// Logisim project adder-test.circ as structural Verilog: 2 circuits, main circuit main
module main (
  output [1:0] a,
  output [1:0] b,
  output [2:0] c,
  output halt
);

  wire clock_1_out;

  Clock clock_1 (.out(clock_1_out));
  Counter #(.width(4), .max('hf)) counter_1 (.Q({b, a}), .carry(halt), .clk(clock_1_out));  // open: load, D, count, clr
  adder_master_main main_1 (.a(a), .b(b), .sum(c));
endmodule

module _2_bit_adder (
  input  [1:0] a,
  input  [1:0] b,
  output [2:0] out_3
);

  Adder #(.width(2)) adder_1 (.a(a), .b(b), .out(out_3[1:0]), .cout(out_3[2]));  // open: cin
endmodule
