// Logisim project lab02.circ as structural Verilog: 3 circuits, main circuit 8-8
module _8_6 (
  input  a,
  input  b,
  input  carry,
  output sum,
  output carry_2
);

  wire and_1_out, and_2_out, and_3_out, and_4_out, and_5_out, and_6_out, and_7_out, not_1_out, not_2_out,
       not_3_out, not_4_out, not_5_out, not_6_out;

  not not_1 (not_1_out, a);
  not not_2 (not_2_out, b);
  not not_3 (not_3_out, a);
  not not_4 (not_4_out, carry);
  not not_5 (not_5_out, b);
  not not_6 (not_6_out, carry);
  and and_1 (and_1_out, b, carry);
  and and_2 (and_2_out, a, carry);
  and and_3 (and_3_out, a, b);
  and and_4 (and_4_out, not_1_out, not_2_out, carry);
  and and_5 (and_5_out, not_3_out, b, not_4_out);
  and and_6 (and_6_out, a, not_5_out, not_6_out);
  and and_7 (and_7_out, a, b, carry);
  or or_1 (carry_2, and_1_out, and_2_out, and_3_out);
  or or_2 (sum, and_4_out, and_5_out, and_6_out, and_7_out);
endmodule

module _8_8 (
);

  RAM ram_1 ();  // open: addr, data, sel, clk, ld, clr
  ROM rom_1 ();  // open: addr, data, sel
endmodule

module _8_9 (
  input  reset,
  output [3:0] count
);

  wire clock_out;
  wire [3:0] adder_1_out, multiplexer_1_out;

  // Probe on adder_1_out
  Multiplexer #(.width(4)) multiplexer_1 (
    .in0(adder_1_out), .in1(4'b0000), .out(multiplexer_1_out), .sel(reset));  // open: en
  Register #(.width(4)) register_1 (.D(multiplexer_1_out), .Q(count), .clk(clock_out));  // open: en, clr
  Clock clock (.out(clock_out));
  Adder #(.width(4)) adder_1 (.a(count), .b(4'b0001), .out(adder_1_out));  // open: cin, cout
endmodule
