// Logisim project lab01.circ as structural Verilog: 6 circuits, main circuit 8-1
module _8_1 (
  input  x,
  input  y,
  output out_3
);

  wire and_1_out, and_2_out, not_1_out, not_2_out;

  not not_1 (not_1_out, x);
  not not_2 (not_2_out, y);
  and and_1 (and_1_out, not_1_out, y);
  and and_2 (and_2_out, x, not_2_out);
  or or_1 (out_3, and_1_out, and_2_out);

  // Notes on the sheet:
  //   XOR Circuit
  //   built using Logisim
endmodule

module _8_2 (
  input  in_1,
  input  in_2,
  input  in_3,
  output out_4,
  output out_5,
  output out_6,
  output out_7,
  output out_8,
  output out_9,
  output out_10
);

  wire and_2_out, d_ff_1_qn, not_3_out;

  not not_1 (out_6, in_1);
  not not_2 (out_9, in_2);
  not not_3 (not_3_out, out_10);
  and and_1 (out_5, in_1, out_6);
  and and_2 (and_2_out, in_2, out_9);
  and and_3 (out_10, in_3, not_3_out);
  D_Flip_Flop d_ff_1 (.clk(and_2_out), .D(d_ff_1_qn), .Q(out_8), .Qn(d_ff_1_qn));  // open: preset, en, reset

  assign out_4 = in_1;
  assign out_7 = in_2;
endmodule

module _8_3 (
  input  x,
  input  y,
  output out_3
);

  wire and_4_out, and_5_out, not_1_out, not_2_out;

  // AND_Gate and_1 is placed but not wired
  not not_1 (not_1_out, x);
  not not_2 (not_2_out, y);
  // AND_Gate and_2 is placed but not wired
  // AND_Gate and_3 is placed but not wired
  and and_4 (and_4_out, not_1_out, y);
  and and_5 (and_5_out, x, not_2_out);
  // AND_Gate and_6 is placed but not wired
  // AND_Gate and_7 is placed but not wired
  or or_1 (out_3, and_4_out, and_5_out);

  // Notes on the sheet:
  //   XOR Circuit
  //   built using Logisim
endmodule

module _8_4_2_1MUX (
  input  in_0,
  input  in_1,
  input  select,
  output out_4
);

  wire and_1_out, and_2_out, not_1_out;

  not not_1 (not_1_out, select);
  and and_1 (and_1_out, in_0, not_1_out);
  and and_2 (and_2_out, in_1, select);
  or or_1 (out_4, and_1_out, and_2_out);
endmodule

module _8_4_4_1MUX (
  input  in_00,
  input  in_01,
  input  in_10,
  input  in_11,
  input  sel_0,
  input  sel1,
  output out_7
);

  wire n8_4_2_1mux_1_out_4, n8_4_2_1mux_2_out_4;

  _8_4_2_1MUX u_8_4_2_1mux_1 (.in_0(in_00), .in_1(in_01), .out_4(n8_4_2_1mux_1_out_4), .select(sel1));
  _8_4_2_1MUX u_8_4_2_1mux_2 (.in_0(in_10), .in_1(in_11), .out_4(n8_4_2_1mux_2_out_4), .select(sel1));
  _8_4_2_1MUX u_8_4_2_1mux_3 (.in_0(n8_4_2_1mux_1_out_4), .in_1(n8_4_2_1mux_2_out_4), .out_4(out_7), .select(sel_0));
endmodule

module _8_5 (
  input  [2:0] in_1,
  input  [2:0] in_2,
  input  [7:0] in_3,
  input  in_4,
  output [2:0] out_5,
  output [3:0] out_6,
  output out_7
);

  assign out_5 = in_1 & in_2;  // AND_Gate and_1, 3 bits wide
  // Probe on in_3[3:0]
  assign out_6 = in_3[3:0] & in_3[7:4];  // AND_Gate and_2, 4 bits wide
  // Probe on in_3[7:4]

  assign out_7 = in_4;
endmodule
