// Logisim project adder-query.circ as structural Verilog: 3 circuits, main circuit main
module main (
  input  [1:0] in_1,
  input  [1:0] in_2,
  output [2:0] out_3
);

  HA ha_1 (.a(in_1[0]), .b(in_2[0]), .sum(out_3[0]));  // open: cout
  FA fa_1 (.A(in_1[1]), .B(in_2[1]), .Sum(out_3[1]), .Cout(out_3[2]));  // open: Cin
endmodule

module HA (
  input  a,
  input  b,
  output sum,
  output cout
);

  xor xor_1 (sum, a, b);
  and and_1 (cout, a, b);
endmodule

module FA (
  input  Cin,
  input  A,
  input  B,
  output Sum,
  output Cout
);

  wire and_1_out, and_2_out, xor_1_out;

  and and_1 (and_1_out, A, B);
  xor xor_1 (xor_1_out, A, B);
  and and_2 (and_2_out, xor_1_out, Cin);
  xor xor_2 (Sum, Cin, xor_1_out);
  or or_1 (Cout, and_1_out, and_2_out);
endmodule
