// Logisim project cpu.circ as structural Verilog: 1 circuit, main circuit main
module main (
  output [7:0] data_out,
  output halt,
  output [3:0] addr_out
);

  wire clock_1_out;

  Counter #(.width(4), .max('hf), .trigger("falling")) counter_1 (
    .Q(addr_out), .carry(halt), .clk(clock_1_out));  // open: load, D, count, clr
  Clock clock_1 (.out(clock_1_out));
  RAM #(.addrWidth(4), .bus("separate")) ram_1 (
    .addr(addr_out), .data(data_out), .ld(1'b1));  // open: din, str, sel, clk, clr
endmodule
